// Logisim project Circuiti.circ as structural Verilog: 18 circuits, main circuit main
module main (
);

  wire B, Clear, coloridisplay_1_out_2, coloridisplay_1_out_3, coloridisplay_1_out_4, coloridisplay_1_out_5,
       coloridisplay_1_out_6, coloridisplay_1_out_7, coloridisplay_1_out_8, coloridisplay_1_out_9,
       coloridisplay_1_out_10, comparator_1_eq, comparator_2_eq, Difficile, Facile, G, or_1_out, R,
       Reset_Punteggio, Start_New_Game, Tempo, Vittoria;
  wire [1:0] Disegno;
  wire [3:0] BombeDisinnescate, DSecondi, Input_Indovinati, USecondi;
  wire [5:0] Codice_di_sblocco, \input ;
  wire [31:0] _1, _2, _3, _4, _5, _6, _7, _8, _9, _10, _11, _12, _13, _14, _15, _16, _17, _18, _19, _20, _21,
       _22, _23, _24, _25, _26, _27, _28, _29, _30, _31, _32, _33, _34, _35, _36, _37, _38, _39,
       bombafissa_1__0, bombafissa_1__1, bombafissa_1__2, bombafissa_1__3, bombafissa_1__4, bombafissa_1__5,
       bombafissa_1__6, bombafissa_1__7, bombafissa_1__8, bombafissa_1__9, bombafissa_1__10,
       bombafissa_1__11, bombafissa_1__12, bombafissa_1__13, bombafissa_1__14, bombafissa_1__15,
       bombafissa_1__16, bombafissa_1__17, bombafissa_1__18, bombafissa_1__19, bombafissa_1__20,
       bombafissa_1__21, bombafissa_1__22, bombafissa_1__23, bombafissa_1__24, bombafissa_1__25,
       bombafissa_1__26, bombafissa_1__27, bombafissa_1__28, bombafissa_1__29, bombafissa_1__30,
       bombafissa_1__31, gameover_1_out_1, gameover_1_out_2, gameover_1_out_3, gameover_1_out_4,
       gameover_1_out_5, gameover_1_out_6, gameover_1_out_7, gameover_1_out_8, gameover_1_out_9,
       gameover_1_out_10, gameover_1_out_11, gameover_1_out_12, gameover_1_out_13, gameover_1_out_14,
       gameover_1_out_15, gameover_1_out_16, gameover_1_out_17, gameover_1_out_18, gameover_1_out_19,
       gameover_1_out_20, gameover_1_out_21, gameover_1_out_22, gameover_1_out_23, gameover_1_out_24,
       gameover_1_out_25, gameover_1_out_26, gameover_1_out_27, gameover_1_out_28, gameover_1_out_29,
       gameover_1_out_30, gameover_1_out_31, gameover_1_out_32, gamewin_1_out_1, gamewin_1_out_2,
       gamewin_1_out_3, gamewin_1_out_4, gamewin_1_out_5, gamewin_1_out_6, gamewin_1_out_7, gamewin_1_out_8,
       gamewin_1_out_9, gamewin_1_out_10, gamewin_1_out_11, gamewin_1_out_12, gamewin_1_out_13,
       gamewin_1_out_14, gamewin_1_out_15, gamewin_1_out_16, gamewin_1_out_17, gamewin_1_out_18,
       gamewin_1_out_19, gamewin_1_out_20, gamewin_1_out_21, gamewin_1_out_22, gamewin_1_out_23,
       gamewin_1_out_24, gamewin_1_out_25, gamewin_1_out_26, gamewin_1_out_27, gamewin_1_out_28,
       gamewin_1_out_29, gamewin_1_out_30, gamewin_1_out_31, gamewin_1_out_32, in_game_1_out_1,
       in_game_1_out_2, in_game_1_out_3, in_game_1_out_4, in_game_1_out_5, in_game_1_out_6, in_game_1_ultimo,
       lost_1_out_1, lost_1_out_2, lost_1_out_3, lost_1_out_4, lost_1_out_5, lost_1_out_6, lost_1_ultimo,
       won_1_out_1, won_1_out_2, won_1_out_3, won_1_out_4, won_1_out_5, won_1_out_6, won_1_ultimo;

  BombaFissa bombafissa_1 (
    ._1(bombafissa_1__1), ._9(bombafissa_1__9), ._2(bombafissa_1__2), ._0(bombafissa_1__0),
    ._10(bombafissa_1__10), ._3(bombafissa_1__3), ._11(bombafissa_1__11), ._4(bombafissa_1__4),
    ._12(bombafissa_1__12), ._5(bombafissa_1__5), ._13(bombafissa_1__13), ._6(bombafissa_1__6),
    ._14(bombafissa_1__14), ._7(bombafissa_1__7), ._15(bombafissa_1__15), ._8(bombafissa_1__8),
    ._16(bombafissa_1__16), ._17(bombafissa_1__17), ._25(bombafissa_1__25), ._18(bombafissa_1__18),
    ._26(bombafissa_1__26), ._19(bombafissa_1__19), ._27(bombafissa_1__27), ._20(bombafissa_1__20),
    ._28(bombafissa_1__28), ._21(bombafissa_1__21), ._29(bombafissa_1__29), ._22(bombafissa_1__22),
    ._30(bombafissa_1__30), ._23(bombafissa_1__23), ._31(bombafissa_1__31), ._24(bombafissa_1__24));
  Button button_1 (.out(Difficile));
  Button button_2 (.out(Facile));
  Button button_3 (.out(R));
  SequenzaInput sequenzainput_1 (.R(R), .G(G), .B(B), .Clear(or_1_out), .out_5(\input ));
  or or_1 (or_1_out, Clear, Start_New_Game);
  BombeDisinnescate bombedisinnescate_1 (
    .Vittoria(Vittoria), .Reset_Puntegio(Reset_Punteggio), .out_3(BombeDisinnescate));
  Hex_Digit_Display hex_digit_display_1 (.value(DSecondi));  // open: dp
  Hex_Digit_Display hex_digit_display_2 (.value(USecondi));  // open: dp
  LED led_1 (.in(coloridisplay_1_out_10));
  LED led_2 (.in(coloridisplay_1_out_7));
  LED led_3 (.in(coloridisplay_1_out_6));
  LED led_4 (.in(coloridisplay_1_out_9));
  LED led_5 (.in(coloridisplay_1_out_8));
  LED led_6 (.in(coloridisplay_1_out_5));
  Button button_4 (.out(G));
  Button button_5 (.out(Clear));
  Button button_6 (.out(Start_New_Game));
  Button button_7 (.out(Reset_Punteggio));
  ColoriDisplay coloridisplay_1 (
    .in_1(\input ), .out_2(coloridisplay_1_out_2), .out_3(coloridisplay_1_out_3),
    .out_4(coloridisplay_1_out_4), .out_5(coloridisplay_1_out_5), .out_6(coloridisplay_1_out_6),
    .out_7(coloridisplay_1_out_7), .out_8(coloridisplay_1_out_8), .out_9(coloridisplay_1_out_9),
    .out_10(coloridisplay_1_out_10));
  LED led_7 (.in(coloridisplay_1_out_4));
  LED led_8 (.in(coloridisplay_1_out_3));
  LED led_9 (.in(coloridisplay_1_out_2));
  Button button_8 (.out(B));
  Hex_Digit_Display hex_digit_display_3 (.value(BombeDisinnescate));  // open: dp
  Hex_Digit_Display hex_digit_display_4 (.value(Input_Indovinati));  // open: dp
  GeneraSequenza generasequenza_1 (.in_1(Start_New_Game), .out_2(Codice_di_sblocco));
  GameOver gameover_1 (
    .out_1(gameover_1_out_1), .out_2(gameover_1_out_2), .out_3(gameover_1_out_3), .out_4(gameover_1_out_4),
    .out_5(gameover_1_out_5), .out_6(gameover_1_out_6), .out_7(gameover_1_out_7), .out_8(gameover_1_out_8),
    .out_9(gameover_1_out_9), .out_10(gameover_1_out_10), .out_11(gameover_1_out_11),
    .out_12(gameover_1_out_12), .out_13(gameover_1_out_13), .out_14(gameover_1_out_14),
    .out_15(gameover_1_out_15), .out_16(gameover_1_out_16), .out_17(gameover_1_out_17),
    .out_18(gameover_1_out_18), .out_19(gameover_1_out_19), .out_20(gameover_1_out_20),
    .out_21(gameover_1_out_21), .out_22(gameover_1_out_22), .out_23(gameover_1_out_23),
    .out_24(gameover_1_out_24), .out_25(gameover_1_out_25), .out_26(gameover_1_out_26),
    .out_27(gameover_1_out_27), .out_28(gameover_1_out_28), .out_29(gameover_1_out_29),
    .out_30(gameover_1_out_30), .out_31(gameover_1_out_31), .out_32(gameover_1_out_32));
  CountDown countdown_1 (
    .Difficile(Difficile), .Facile(Facile), .Decina(DSecondi), .\Unità (USecondi), .Vittoria(Vittoria));
  DecideDisegno decidedisegno_1 (
    .Disegno(Disegno), .in_2(bombafissa_1__0), .in_3(bombafissa_1__1), .in_4(bombafissa_1__2),
    .in_5(bombafissa_1__3), .in_6(bombafissa_1__4), .in_7(bombafissa_1__5), .in_8(bombafissa_1__6),
    .in_9(bombafissa_1__7), .in_10(bombafissa_1__8), .in_11(bombafissa_1__9), .in_12(bombafissa_1__10),
    .in_13(bombafissa_1__11), .in_14(bombafissa_1__12), .in_15(bombafissa_1__13), .in_16(bombafissa_1__14),
    .in_17(bombafissa_1__15), .in_18(bombafissa_1__16), .in_19(bombafissa_1__17), .in_20(bombafissa_1__18),
    .in_21(bombafissa_1__19), .in_22(bombafissa_1__20), .in_23(bombafissa_1__21), .in_24(bombafissa_1__22),
    .in_25(bombafissa_1__23), .in_26(bombafissa_1__24), .in_27(bombafissa_1__25), .in_28(bombafissa_1__26),
    .in_29(bombafissa_1__27), .in_30(bombafissa_1__28), .in_31(bombafissa_1__29), .in_32(bombafissa_1__30),
    .in_33(bombafissa_1__31), .in_34(gameover_1_out_1), .in_35(gameover_1_out_2), .in_36(gameover_1_out_3),
    .in_37(gameover_1_out_4), .in_38(gameover_1_out_5), .in_39(gameover_1_out_6), .in_40(gameover_1_out_7),
    .in_41(gameover_1_out_8), .in_42(gameover_1_out_9), .in_43(gameover_1_out_10), .in_44(gameover_1_out_11),
    .in_45(gameover_1_out_12), .in_46(gameover_1_out_13), .in_47(gameover_1_out_14),
    .in_48(gameover_1_out_15), .in_49(gameover_1_out_16), .in_50(gameover_1_out_17),
    .in_51(gameover_1_out_18), .in_52(gameover_1_out_19), .in_53(gameover_1_out_20),
    .in_54(gameover_1_out_21), .in_55(gameover_1_out_22), .in_56(gameover_1_out_23),
    .in_57(gameover_1_out_24), .in_58(gameover_1_out_25), .in_59(gameover_1_out_26),
    .in_60(gameover_1_out_27), .in_61(gameover_1_out_28), .in_62(gameover_1_out_29),
    .in_63(gameover_1_out_30), .in_64(gameover_1_out_31), .in_65(gameover_1_out_32), .in_66(gamewin_1_out_1),
    .in_67(gamewin_1_out_2), .in_68(gamewin_1_out_3), .in_69(gamewin_1_out_4), .in_70(gamewin_1_out_5),
    .in_71(gamewin_1_out_6), .in_72(gamewin_1_out_7), .in_73(gamewin_1_out_8), .in_74(gamewin_1_out_9),
    .in_75(gamewin_1_out_10), .in_76(gamewin_1_out_11), .in_77(gamewin_1_out_12), .in_78(gamewin_1_out_13),
    .in_79(gamewin_1_out_14), .in_80(gamewin_1_out_15), .in_81(gamewin_1_out_16), .in_82(gamewin_1_out_17),
    .in_83(gamewin_1_out_18), .in_84(gamewin_1_out_19), .in_85(gamewin_1_out_20), .in_86(gamewin_1_out_21),
    .in_87(gamewin_1_out_22), .in_88(gamewin_1_out_23), .in_89(gamewin_1_out_24), .in_90(gamewin_1_out_25),
    .in_91(gamewin_1_out_26), .in_92(gamewin_1_out_27), .in_93(gamewin_1_out_28), .in_94(gamewin_1_out_29),
    .in_95(gamewin_1_out_30), .in_96(gamewin_1_out_31), .in_97(gamewin_1_out_32), .in_98(in_game_1_out_1),
    .in_99(in_game_1_out_2), .in_100(in_game_1_out_3), .in_101(in_game_1_out_4), .in_102(in_game_1_out_5),
    .in_103(in_game_1_out_6), .ultimo_in_game(in_game_1_ultimo), .in_105(lost_1_out_1),
    .in_106(lost_1_out_2), .in_107(lost_1_out_3), .in_108(lost_1_out_4), .in_109(lost_1_out_5),
    .in_110(lost_1_out_6), .ultimo_lost(lost_1_ultimo), .in_112(won_1_out_1), .in_113(won_1_out_2),
    .in_114(won_1_out_3), .in_115(won_1_out_4), .in_116(won_1_out_5), .in_117(won_1_out_6),
    .ultimo_won(won_1_ultimo), .out_119(_1), .out_120(_2), .out_121(_3), .out_122(_4), .out_123(_5),
    .out_124(_6), .out_125(_7), .out_126(_8), .out_127(_9), .out_128(_10), .out_129(_11), .out_130(_12),
    .out_131(_13), .out_132(_14), .out_133(_15), .out_134(_16), .out_135(_17), .out_136(_18), .out_137(_19),
    .out_138(_20), .out_139(_21), .out_140(_22), .out_141(_23), .out_142(_24), .out_143(_25), .out_144(_26),
    .out_145(_27), .out_146(_28), .out_147(_29), .out_148(_30), .out_149(_31), .out_150(_32), .out_151(_33),
    .out_152(_34), .out_153(_35), .out_154(_36), .out_155(_37), .out_156(_38), .ultimo(_39));
  DotMatrix #(.matrixcols(7), .matrixrows(32)) dotmatrix_1 (
    .col0(_33), .col1(_34), .col2(_35), .col3(_36), .col4(_37), .col5(_38), .col6(_39));
  DotMatrix #(.matrixcols(32), .matrixrows(32)) dotmatrix_2 (
    .col0(_1), .col1(_2), .col2(_3), .col3(_4), .col4(_5), .col5(_6), .col6(_7), .col7(_8), .col8(_9),
    .col9(_10), .col10(_11), .col11(_12), .col12(_13), .col13(_14), .col14(_15), .col15(_16), .col16(_17),
    .col17(_18), .col18(_19), .col19(_20), .col20(_21), .col21(_22), .col22(_23), .col23(_24), .col24(_25),
    .col25(_26), .col26(_27), .col27(_28), .col28(_29), .col29(_30), .col30(_31), .col31(_32));
  ControllaVittoria controllavittoria_1 (.in_1(\input ), .in_2(Codice_di_sblocco), .out_3(Vittoria));
  Comparator #(.width(4), .mode("unsigned")) comparator_1 (
    .a(USecondi), .b(4'b0000), .eq(comparator_1_eq));  // open: gt, lt
  Comparator #(.width(4), .mode("unsigned")) comparator_2 (
    .a(DSecondi), .b(4'b0000), .eq(comparator_2_eq));  // open: gt, lt
  GameWin gamewin_1 (
    .out_1(gamewin_1_out_1), .out_2(gamewin_1_out_2), .out_3(gamewin_1_out_3), .out_4(gamewin_1_out_4),
    .out_5(gamewin_1_out_5), .out_6(gamewin_1_out_6), .out_7(gamewin_1_out_7), .out_8(gamewin_1_out_8),
    .out_9(gamewin_1_out_9), .out_10(gamewin_1_out_10), .out_11(gamewin_1_out_11), .out_12(gamewin_1_out_12),
    .out_13(gamewin_1_out_13), .out_14(gamewin_1_out_14), .out_15(gamewin_1_out_15),
    .out_16(gamewin_1_out_16), .out_17(gamewin_1_out_17), .out_18(gamewin_1_out_18),
    .out_19(gamewin_1_out_19), .out_20(gamewin_1_out_20), .out_21(gamewin_1_out_21),
    .out_22(gamewin_1_out_22), .out_23(gamewin_1_out_23), .out_24(gamewin_1_out_24),
    .out_25(gamewin_1_out_25), .out_26(gamewin_1_out_26), .out_27(gamewin_1_out_27),
    .out_28(gamewin_1_out_28), .out_29(gamewin_1_out_29), .out_30(gamewin_1_out_30),
    .out_31(gamewin_1_out_31), .out_32(gamewin_1_out_32));
  and and_1 (Tempo, comparator_1_eq, comparator_2_eq);
  InputIndovinati inputindovinati_1 (.in_1(\input ), .in_2(Codice_di_sblocco), .out_3(Input_Indovinati));
  FSM_grafica fsm_grafica_1 (.out_3(Disegno), .Vittoria(Vittoria), .Tempo(Tempo));
  in_game in_game_1 (
    .out_1(in_game_1_out_1), .out_2(in_game_1_out_2), .out_3(in_game_1_out_3), .out_4(in_game_1_out_4),
    .out_5(in_game_1_out_5), .out_6(in_game_1_out_6), .ultimo(in_game_1_ultimo));
  lost lost_1 (
    .out_1(lost_1_out_1), .out_2(lost_1_out_2), .out_3(lost_1_out_3), .out_4(lost_1_out_4),
    .out_5(lost_1_out_5), .out_6(lost_1_out_6), .ultimo(lost_1_ultimo));
  won won_1 (
    .out_1(won_1_out_1), .out_2(won_1_out_2), .out_3(won_1_out_3), .out_4(won_1_out_4), .out_5(won_1_out_5),
    .out_6(won_1_out_6), .ultimo(won_1_ultimo));

  // Notes on the sheet:
  //   Scelta livello:
  //   Difficile
  //   Facile
  //   1) Cominciare una nuova partita con Start New Game
  //   2) Selezionare la difficoltà tramite i livelli
  //   3) Indovinare il codice grazie all'aiuto degli input indovinati
  //   Scrive l'input
  //   Bombe disinnescate
  //   Secondi all'esplosione:
  //   0) Impostare Zoom a 150%, Tick Frequency a 128 Hz e premere Ctrl+K per far partire il clock 
  //   Cancella il codice messo in input
  //   Quante bombe
  //   hai disinnescato:
  //   Quanti input
  //   hai indovinato:
  //   Comincia una nuova partita
  //   con un nuovo codice da indovinare
  //   Porta a 0 il numero di bombe disinnescate
  //   Genera nuovo codice da indovinare
  //   Scelta livello e CoundDown
  //   Controlla se l'input è uguale al codice di sblocco
  //   Controlla che il tempo sia scaduto
  //   Dalla situazione sceglie il disegno da rappresentare
  //   (vittoria, sconfitta, in corso)
  //   Input indovinati
  //   FSM che decide la situazione
endmodule

module SequenzaInput (
  input  R,
  input  G,
  input  B,
  input  Clear,
  output [5:0] out_5
);

  wire and_4_out, and_5_out, and_6_out, clock_1_out, clock_2_out, clock_3_out, comparator_1_eq,
       comparator_2_eq, comparator_3_eq, controlled_buffer_1_out, controlled_buffer_2_out,
       controlled_buffer_3_out, or_1_out, or_3_out, or_4_out, or_5_out, undriven;
  wire [1:0] and_1_out, and_2_out, and_3_out, multiplexer_1_out, multiplexer_2_out, multiplexer_3_out,
       multiplexer_4_out, multiplexer_5_out, multiplexer_6_out, or_2_out;
  wire [7:0] counter_1_q;

  assign and_1_out = {2{R}} & 2'b01;  // AND_Gate and_1, 2 bits wide
  assign and_2_out = {2{G}} & 2'b10;  // AND_Gate and_2, 2 bits wide
  assign and_3_out = {2{B}} & 2'b11;  // AND_Gate and_3, 2 bits wide
  or or_1 (or_1_out, B, R, G);
  assign or_2_out = and_1_out | and_2_out | and_3_out;  // OR_Gate or_2, 2 bits wide
  Counter counter_1 (.Q(counter_1_q), .clk(or_1_out), .clr(Clear));  // open: load, D, count, carry
  Comparator #(.mode("unsigned")) comparator_1 (.a(counter_1_q), .b(8'h3), .eq(comparator_1_eq));  // open: gt, lt
  Comparator #(.mode("unsigned")) comparator_2 (.a(counter_1_q), .b(8'h1), .eq(comparator_2_eq));  // open: gt, lt
  and and_4 (and_4_out, or_1_out, comparator_3_eq);
  Comparator #(.mode("unsigned")) comparator_3 (.a(counter_1_q), .b(8'h2), .eq(comparator_3_eq));  // open: gt, lt
  and and_5 (and_5_out, or_1_out, comparator_1_eq);
  Multiplexer #(.width(2)) multiplexer_1 (
    .in1(or_2_out), .out(multiplexer_1_out), .sel(and_5_out), .en(undriven));  // open: in0
  and and_6 (and_6_out, or_1_out, comparator_2_eq);
  Multiplexer #(.width(2)) multiplexer_2 (.in1(or_2_out), .out(multiplexer_2_out), .sel(and_6_out));  // open: in0, en
  Multiplexer #(.width(2)) multiplexer_3 (
    .in0(multiplexer_2_out), .in1(2'b00), .out(multiplexer_3_out), .sel(Clear));  // open: en
  Multiplexer #(.width(2)) multiplexer_4 (.in1(or_2_out), .out(multiplexer_4_out), .sel(and_4_out));  // open: in0, en
  Multiplexer #(.width(2)) multiplexer_5 (
    .in0(multiplexer_4_out), .in1(2'b00), .out(multiplexer_5_out), .sel(Clear));  // open: en
  Multiplexer #(.width(2)) multiplexer_6 (
    .in0(multiplexer_1_out), .in1(2'b00), .out(multiplexer_6_out), .sel(Clear));  // open: en
  Register #(.width(2)) register_1 (
    .D(multiplexer_3_out), .Q(out_5[5:4]), .clk(controlled_buffer_1_out));  // open: en, clr
  assign controlled_buffer_1_out = or_3_out ? clock_1_out : 1'bz;  // Controlled_Buffer controlled_buffer_1
  or or_3 (or_3_out, and_6_out, Clear);
  Clock clock_1 (.out(clock_1_out));
  Register #(.width(2)) register_2 (
    .D(multiplexer_5_out), .Q(out_5[3:2]), .clk(controlled_buffer_2_out));  // open: en, clr
  assign controlled_buffer_2_out = or_4_out ? clock_2_out : 1'bz;  // Controlled_Buffer controlled_buffer_2
  or or_4 (or_4_out, and_4_out, Clear);
  Clock clock_2 (.out(clock_2_out));
  Register #(.width(2)) register_3 (
    .D(multiplexer_6_out), .Q(out_5[1:0]), .clk(controlled_buffer_3_out));  // open: en, clr
  assign controlled_buffer_3_out = or_5_out ? clock_3_out : 1'bz;  // Controlled_Buffer controlled_buffer_3
  or or_5 (or_5_out, and_5_out, Clear);
  Clock clock_3 (.out(clock_3_out));
endmodule

module ColoriDisplay (
  input  [5:0] in_1,
  output out_2,
  output out_3,
  output out_4,
  output out_5,
  output out_6,
  output out_7,
  output out_8,
  output out_9,
  output out_10
);

  Comparator #(.width(2), .mode("unsigned")) comparator_1 (.a(in_1[1:0]), .b(2'b11), .eq(out_2));  // open: gt, lt
  Comparator #(.width(2), .mode("unsigned")) comparator_2 (.a(in_1[1:0]), .b(2'b10), .eq(out_3));  // open: gt, lt
  Comparator #(.width(2), .mode("unsigned")) comparator_3 (.a(in_1[1:0]), .b(2'b01), .eq(out_4));  // open: gt, lt
  Comparator #(.width(2), .mode("unsigned")) comparator_4 (.a(in_1[3:2]), .b(2'b11), .eq(out_5));  // open: gt, lt
  Comparator #(.width(2), .mode("unsigned")) comparator_5 (.a(in_1[3:2]), .b(2'b10), .eq(out_6));  // open: gt, lt
  Comparator #(.width(2), .mode("unsigned")) comparator_6 (.a(in_1[3:2]), .b(2'b01), .eq(out_7));  // open: gt, lt
  Comparator #(.width(2), .mode("unsigned")) comparator_7 (.a(in_1[5:4]), .b(2'b11), .eq(out_8));  // open: gt, lt
  Comparator #(.width(2), .mode("unsigned")) comparator_8 (.a(in_1[5:4]), .b(2'b10), .eq(out_9));  // open: gt, lt
  Comparator #(.width(2), .mode("unsigned")) comparator_9 (.a(in_1[5:4]), .b(2'b01), .eq(out_10));  // open: gt, lt
endmodule

module GeneraSequenza (
  input  in_1,
  output [5:0] out_2
);

  wire comparator_1_eq, comparator_2_eq, comparator_3_eq;
  wire [1:0] multiplexer_1_out, multiplexer_3_out, multiplexer_5_out, random_1_out, random_2_out,
       random_3_out;

  Random #(.width(2), .seed(1)) random_1 (.clk(in_1), .out(random_1_out));  // open: next, clr
  Random #(.width(2), .seed(3)) random_2 (.clk(in_1), .out(random_2_out));  // open: next, clr
  Random #(.width(2)) random_3 (.clk(in_1), .out(random_3_out));  // open: next, clr
  Comparator #(.width(2), .mode("unsigned")) comparator_1 (
    .a(random_3_out), .b(2'b00), .eq(comparator_1_eq));  // open: gt, lt
  Comparator #(.width(2), .mode("unsigned")) comparator_2 (
    .a(random_1_out), .b(2'b00), .eq(comparator_2_eq));  // open: gt, lt
  Comparator #(.width(2), .mode("unsigned")) comparator_3 (
    .a(random_2_out), .b(2'b00), .eq(comparator_3_eq));  // open: gt, lt
  Multiplexer #(.width(2)) multiplexer_1 (
    .in1(random_3_out), .out(multiplexer_1_out), .sel(comparator_1_eq));  // open: in0, en
  Multiplexer #(.width(2)) multiplexer_2 (
    .in0(random_3_out), .out(out_2[1:0]), .sel(comparator_1_eq));  // open: in1, en
  Multiplexer #(.width(2)) multiplexer_3 (
    .in1(random_1_out), .out(multiplexer_3_out), .sel(comparator_2_eq));  // open: in0, en
  Multiplexer #(.width(2)) multiplexer_4 (
    .in0(random_1_out), .out(out_2[3:2]), .sel(comparator_2_eq));  // open: in1, en
  Multiplexer #(.width(2)) multiplexer_5 (
    .in1(random_2_out), .out(multiplexer_5_out), .sel(comparator_3_eq));  // open: in0, en
  Multiplexer #(.width(2)) multiplexer_6 (
    .in0(random_2_out), .out(out_2[5:4]), .sel(comparator_3_eq));  // open: in1, en
  Adder #(.width(2)) adder_1 (.a(multiplexer_1_out), .b(2'b01), .out(out_2[1:0]));  // open: cin, cout
  Adder #(.width(2)) adder_2 (.a(multiplexer_3_out), .b(2'b01), .out(out_2[3:2]));  // open: cin, cout
  Adder #(.width(2)) adder_3 (.a(multiplexer_5_out), .b(2'b01), .out(out_2[5:4]));  // open: cin, cout
endmodule

module ControllaVittoria (
  input  [5:0] in_1,
  input  [5:0] in_2,
  output out_3
);

  Comparator #(.width(6), .mode("unsigned")) comparator_1 (.a(in_1), .b(in_2), .eq(out_3));  // open: gt, lt
endmodule

module InputIndovinati (
  input  [5:0] in_1,
  input  [5:0] in_2,
  output [3:0] out_3
);

  wire comparator_1_eq;
  wire [0:0] comparator_2_eq, comparator_3_eq;

  Comparator #(.width(2)) comparator_1 (.a(in_1[1:0]), .b(in_2[1:0]), .eq(comparator_1_eq));  // open: gt, lt
  Comparator #(.width(2)) comparator_2 (.a(in_1[3:2]), .b(in_2[3:2]), .eq(comparator_2_eq[0]));  // open: gt, lt
  Comparator #(.width(2)) comparator_3 (.a(in_1[5:4]), .b(in_2[5:4]), .eq(comparator_3_eq[0]));  // open: gt, lt
  Adder #(.width(2)) adder_1 (
    .a({1'b0, comparator_2_eq[0]}), .b({1'b0, comparator_3_eq[0]}), .out(out_3[1:0]), .cin(comparator_1_eq));  // open: cout

  assign out_3[3:2] = 2'b00;
endmodule

module CountDown (
  input  Vittoria,
  input  Difficile,
  input  Facile,
  output [3:0] Decina,
  output [3:0] \Unità 
);

  wire clock_1_out, clock_2_out, clock_3_out, clock_4_out, comparator_1_eq, comparator_1_gt, comparator_1_lt,
       controlled_buffer_1_out, controlled_buffer_2_out, controlled_buffer_3_out, controlled_buffer_4_out,
       counter_1_carry, counter_2_carry, counter_3_carry, counter_4_carry, not_1_out, not_2_out, not_3_out,
       not_4_out, or_1_out, or_2_out, or_3_out, or_5_out, or_6_out;
  wire [2:0] counter_2_q;
  wire [3:0] counter_3_q, Decina_out, DecinaFacile, multiplexer_2_out, multiplexer_3_out, multiplexer_4_out,
       subtractor_1_out, subtractor_2_out, subtractor_3_out, \Unità_out , \UnitàFacile ;

  Counter #(.width(6), .max('h3f)) counter_1 (
    .load(1'b1), .count(1'b1), .carry(counter_1_carry), .clk(controlled_buffer_1_out), .clr(Difficile));  // open: D, Q
  assign controlled_buffer_1_out = not_1_out ? clock_1_out : 1'bz;  // Controlled_Buffer controlled_buffer_1
  not not_1 (not_1_out, or_2_out);
  Clock clock_1 (.out(clock_1_out));
  Counter #(.width(3), .max('h7)) counter_2 (
    .load(1'b1), .D(3'b000), .count(1'b1), .Q(counter_2_q), .carry(counter_2_carry), .clk(counter_1_carry),
    .clr(or_1_out));
  or or_1 (or_1_out, Vittoria, Difficile);
  or or_2 (or_2_out, counter_2_carry, Vittoria);
  Register #(.width(4)) register_1 (
    .D(Decina_out), .Q(Decina), .clk(controlled_buffer_2_out), .clr(or_3_out));  // open: en
  assign controlled_buffer_2_out = not_2_out ? clock_2_out : 1'bz;  // Controlled_Buffer controlled_buffer_2
  not not_2 (not_2_out, Vittoria);
  Clock clock_2 (.out(clock_2_out));
  assign Decina_out = DecinaFacile;  // OR_Gate Decina, 4 bits wide OR_Gate
  Register #(.width(4)) register_2 (.D(\Unità_out ), .Q(\Unità ), .clk(controlled_buffer_3_out));  // open: en, clr
  assign controlled_buffer_3_out = not_3_out ? clock_3_out : 1'bz;  // Controlled_Buffer controlled_buffer_3
  not not_3 (not_3_out, Vittoria);
  Clock clock_3 (.out(clock_3_out));
  assign \Unità_out  = {1'b0, counter_2_q} | \UnitàFacile ;  // OR_Gate Unità, 4 bits wide
  Subtractor #(.width(4)) subtractor_1 (.a(counter_3_q), .b(4'b0001), .out(subtractor_1_out));  // open: bin, bout
  or or_3 (or_3_out, comparator_1_lt, comparator_1_eq);
  Subtractor #(.width(4)) subtractor_2 (
    .a(counter_3_q), .b(subtractor_1_out), .out(subtractor_2_out));  // open: bin, bout
  Multiplexer #(.width(4)) multiplexer_1 (
    .in1(subtractor_2_out), .out(DecinaFacile), .sel(comparator_1_gt));  // open: in0, en
  Multiplexer #(.width(4)) multiplexer_2 (
    .in0(4'b0000), .in1(counter_3_q), .out(multiplexer_2_out), .sel(comparator_1_eq));  // open: en
  Multiplexer #(.width(4)) multiplexer_3 (
    .in0(4'b0000), .in1(counter_3_q), .out(multiplexer_3_out), .sel(comparator_1_lt));  // open: en
  Clock clock_4 (.out(clock_4_out));
  assign \UnitàFacile  = multiplexer_2_out | multiplexer_3_out | multiplexer_4_out;  // OR_Gate or_4, 4 bits wide
  Counter #(.width(4), .max('hf)) counter_3 (
    .load(1'b1), .count(1'b1), .Q(counter_3_q), .carry(counter_3_carry), .clk(counter_4_carry), .clr(or_5_out));  // open: D
  or or_5 (or_5_out, Vittoria, Facile);
  Counter #(.width(6), .max('h3f)) counter_4 (
    .load(1'b1), .count(1'b1), .carry(counter_4_carry), .clk(controlled_buffer_4_out), .clr(Facile));  // open: D, Q
  assign controlled_buffer_4_out = not_4_out ? clock_4_out : 1'bz;  // Controlled_Buffer controlled_buffer_4
  not not_4 (not_4_out, or_6_out);
  or or_6 (or_6_out, counter_3_carry, Vittoria);
  Multiplexer #(.width(4)) multiplexer_4 (
    .in0(4'b0000), .in1(subtractor_3_out), .out(multiplexer_4_out), .sel(comparator_1_gt));  // open: en
  Comparator #(.width(4), .mode("unsigned")) comparator_1 (
    .a(counter_3_q), .b(4'b1001), .gt(comparator_1_gt), .eq(comparator_1_eq), .lt(comparator_1_lt));
  Subtractor #(.width(4)) subtractor_3 (.a(counter_3_q), .b(4'b1010), .out(subtractor_3_out));  // open: bin, bout

  // Notes on the sheet:
  //   Livello Difficile
  //   Livello Facile
endmodule

module BombeDisinnescate (
  input  Vittoria,
  input  Reset_Puntegio,
  output [3:0] out_3
);

  wire comparator_1_eq, or_1_out;

  Counter #(.width(4), .max('hf)) counter_1 (
    .load(1'b0), .count(Vittoria), .Q(out_3), .clk(Vittoria), .clr(or_1_out));  // open: D, carry
  or or_1 (or_1_out, Reset_Puntegio, comparator_1_eq);
  Comparator #(.width(4), .mode("unsigned")) comparator_1 (
    .a(4'b1010), .b(out_3), .eq(comparator_1_eq));  // open: gt, lt
endmodule

module BombaFissa (
  output [31:0] _1,
  output [31:0] _9,
  output [31:0] _2,
  output [31:0] _0,
  output [31:0] _10,
  output [31:0] _3,
  output [31:0] _11,
  output [31:0] _4,
  output [31:0] _12,
  output [31:0] _5,
  output [31:0] _13,
  output [31:0] _6,
  output [31:0] _14,
  output [31:0] _7,
  output [31:0] _15,
  output [31:0] _8,
  output [31:0] _16,
  output [31:0] _17,
  output [31:0] _25,
  output [31:0] _18,
  output [31:0] _26,
  output [31:0] _19,
  output [31:0] _27,
  output [31:0] _20,
  output [31:0] _28,
  output [31:0] _21,
  output [31:0] _29,
  output [31:0] _22,
  output [31:0] _30,
  output [31:0] _23,
  output [31:0] _31,
  output [31:0] _24
);

  DotMatrix #(.matrixcols(32), .matrixrows(32), .persist(1)) dotmatrix_1 (
    .col0({32{1'b0}}), .col1({32{1'b0}}), .col2({32{1'b0}}), .col3(32'h1f800), .col4(32'h60600),
    .col5(32'h180180), .col6(32'h200040), .col7(32'h400020), .col8(32'h800010), .col9(32'h1000008),
    .col10(32'h1000008), .col11(32'h2000004), .col12(32'h2000004), .col13(32'h4000002), .col14(32'hc000002),
    .col15(32'h3c000002), .col16(32'h7c000002), .col17(32'h6c000002), .col18(32'h44000002),
    .col19(32'h62000004), .col20(32'h32000004), .col21(32'h31000008), .col22(32'h19000008),
    .col23(32'h18800010), .col24(32'hc400020), .col25(32'h4200040), .col26(32'h11180180),
    .col27(32'h4060600), .col28(32'ha01f800), .col29({32{1'b0}}), .col30({32{1'b0}}), .col31({32{1'b0}}));

  assign _0 = {32{1'b0}};
  assign _1 = {32{1'b0}};
  assign _2 = {32{1'b0}};
  assign _3 = 32'h1f800;
  assign _4 = 32'h60600;
  assign _5 = 32'h180180;
  assign _6 = 32'h200040;
  assign _7 = 32'h400020;
  assign _8 = 32'h800010;
  assign _9 = 32'h1000008;
  assign _10 = 32'h1000008;
  assign _11 = 32'h2000004;
  assign _12 = 32'h2000004;
  assign _13 = 32'h4000002;
  assign _14 = 32'hc000002;
  assign _15 = 32'h3c000002;
  assign _16 = 32'h7c000002;
  assign _17 = 32'h6c000002;
  assign _18 = 32'h44000002;
  assign _19 = 32'h62000004;
  assign _20 = 32'h32000004;
  assign _21 = 32'h31000008;
  assign _22 = 32'h19000008;
  assign _23 = 32'h18800010;
  assign _24 = 32'hc400020;
  assign _25 = 32'h4200040;
  assign _26 = 32'h11180180;
  assign _27 = 32'h4060600;
  assign _28 = 32'ha01f800;
  assign _29 = {32{1'b0}};
  assign _30 = {32{1'b0}};
  assign _31 = {32{1'b0}};
endmodule

module GameOver (
  output [31:0] out_1,
  output [31:0] out_2,
  output [31:0] out_3,
  output [31:0] out_4,
  output [31:0] out_5,
  output [31:0] out_6,
  output [31:0] out_7,
  output [31:0] out_8,
  output [31:0] out_9,
  output [31:0] out_10,
  output [31:0] out_11,
  output [31:0] out_12,
  output [31:0] out_13,
  output [31:0] out_14,
  output [31:0] out_15,
  output [31:0] out_16,
  output [31:0] out_17,
  output [31:0] out_18,
  output [31:0] out_19,
  output [31:0] out_20,
  output [31:0] out_21,
  output [31:0] out_22,
  output [31:0] out_23,
  output [31:0] out_24,
  output [31:0] out_25,
  output [31:0] out_26,
  output [31:0] out_27,
  output [31:0] out_28,
  output [31:0] out_29,
  output [31:0] out_30,
  output [31:0] out_31,
  output [31:0] out_32
);

  DotMatrix #(.matrixcols(32), .matrixrows(32)) dotmatrix_1 (
    .col0({32{1'b0}}), .col1({32{1'b0}}), .col2({32{1'b0}}), .col3({32{1'b0}}), .col4({32{1'b0}}),
    .col5({32{1'b0}}), .col6(32'hc0), .col7(32'h1c0), .col8(32'h380), .col9(32'h1f80700),
    .col10(32'hfff0e00), .col11(32'hfff0c00), .col12(32'h1f80c00), .col13(32'hc00), .col14(32'hc00),
    .col15(32'hc00), .col16(32'hc00), .col17(32'hc00), .col18(32'hc00), .col19(32'h1f80c00),
    .col20(32'hfff0c00), .col21(32'hfff0e00), .col22(32'h1f80700), .col23(32'h380), .col24(32'h1c0),
    .col25(32'hc0), .col26({32{1'b0}}), .col27({32{1'b0}}), .col28({32{1'b0}}), .col29({32{1'b0}}),
    .col30({32{1'b0}}), .col31({32{1'b0}}));

  assign out_1 = {32{1'b0}};
  assign out_2 = {32{1'b0}};
  assign out_3 = {32{1'b0}};
  assign out_4 = {32{1'b0}};
  assign out_5 = {32{1'b0}};
  assign out_6 = {32{1'b0}};
  assign out_7 = 32'hc0;
  assign out_8 = 32'h1c0;
  assign out_9 = 32'h380;
  assign out_10 = 32'h1f80700;
  assign out_11 = 32'hfff0e00;
  assign out_12 = 32'hfff0c00;
  assign out_13 = 32'h1f80c00;
  assign out_14 = 32'hc00;
  assign out_15 = 32'hc00;
  assign out_16 = 32'hc00;
  assign out_17 = 32'hc00;
  assign out_18 = 32'hc00;
  assign out_19 = 32'hc00;
  assign out_20 = 32'h1f80c00;
  assign out_21 = 32'hfff0c00;
  assign out_22 = 32'hfff0e00;
  assign out_23 = 32'h1f80700;
  assign out_24 = 32'h380;
  assign out_25 = 32'h1c0;
  assign out_26 = 32'hc0;
  assign out_27 = {32{1'b0}};
  assign out_28 = {32{1'b0}};
  assign out_29 = {32{1'b0}};
  assign out_30 = {32{1'b0}};
  assign out_31 = {32{1'b0}};
  assign out_32 = {32{1'b0}};
endmodule

module GameWin (
  output [31:0] out_1,
  output [31:0] out_2,
  output [31:0] out_3,
  output [31:0] out_4,
  output [31:0] out_5,
  output [31:0] out_6,
  output [31:0] out_7,
  output [31:0] out_8,
  output [31:0] out_9,
  output [31:0] out_10,
  output [31:0] out_11,
  output [31:0] out_12,
  output [31:0] out_13,
  output [31:0] out_14,
  output [31:0] out_15,
  output [31:0] out_16,
  output [31:0] out_17,
  output [31:0] out_18,
  output [31:0] out_19,
  output [31:0] out_20,
  output [31:0] out_21,
  output [31:0] out_22,
  output [31:0] out_23,
  output [31:0] out_24,
  output [31:0] out_25,
  output [31:0] out_26,
  output [31:0] out_27,
  output [31:0] out_28,
  output [31:0] out_29,
  output [31:0] out_30,
  output [31:0] out_31,
  output [31:0] out_32
);

  DotMatrix #(.matrixcols(32), .matrixrows(32)) dotmatrix_1 (
    .col0({32{1'b0}}), .col1({32{1'b0}}), .col2({32{1'b0}}), .col3({32{1'b0}}), .col4({32{1'b0}}),
    .col5({32{1'b0}}), .col6(32'h1800), .col7(32'h1c00), .col8(32'he00), .col9(32'h1f80700),
    .col10(32'hfff0380), .col11(32'hfff0180), .col12(32'h1f80180), .col13(32'h180), .col14(32'h180),
    .col15(32'h180), .col16(32'h180), .col17(32'h180), .col18(32'h180), .col19(32'h1f80180),
    .col20(32'hfff0180), .col21(32'hfff0380), .col22(32'h1f80700), .col23(32'he00), .col24(32'h1c00),
    .col25(32'h1800), .col26({32{1'b0}}), .col27({32{1'b0}}), .col28({32{1'b0}}), .col29({32{1'b0}}),
    .col30({32{1'b0}}), .col31({32{1'b0}}));

  assign out_1 = {32{1'b0}};
  assign out_2 = {32{1'b0}};
  assign out_3 = {32{1'b0}};
  assign out_4 = {32{1'b0}};
  assign out_5 = {32{1'b0}};
  assign out_6 = {32{1'b0}};
  assign out_7 = 32'h1800;
  assign out_8 = 32'h1c00;
  assign out_9 = 32'he00;
  assign out_10 = 32'h1f80700;
  assign out_11 = 32'hfff0380;
  assign out_12 = 32'hfff0180;
  assign out_13 = 32'h1f80180;
  assign out_14 = 32'h180;
  assign out_15 = 32'h180;
  assign out_16 = 32'h180;
  assign out_17 = 32'h180;
  assign out_18 = 32'h180;
  assign out_19 = 32'h180;
  assign out_20 = 32'h1f80180;
  assign out_21 = 32'hfff0180;
  assign out_22 = 32'hfff0380;
  assign out_23 = 32'h1f80700;
  assign out_24 = 32'he00;
  assign out_25 = 32'h1c00;
  assign out_26 = 32'h1800;
  assign out_27 = {32{1'b0}};
  assign out_28 = {32{1'b0}};
  assign out_29 = {32{1'b0}};
  assign out_30 = {32{1'b0}};
  assign out_31 = {32{1'b0}};
  assign out_32 = {32{1'b0}};
endmodule

module FSM_grafica (
  input  Vittoria,
  input  Tempo,
  output [1:0] out_3
);

  wire clock_1_out, temponext_1_tempo_next, vittorianext_1_vittoria_next;

  Clock clock_1 (.out(clock_1_out));
  TempoNext temponext_1 (
    .Tempo_next(temponext_1_tempo_next), .stato_0(out_3[1]), .stato_1(out_3[0]), .Vittoria(Vittoria),
    .Tempo(Tempo));
  VittoriaNext vittorianext_1 (
    .Vittoria_next(vittorianext_1_vittoria_next), .stato_0(out_3[1]), .stato_1(out_3[0]),
    .Vittoria(Vittoria), .Tempo(Tempo));
  D_Flip_Flop d_ff_1 (
    .clk(clock_1_out), .D(vittorianext_1_vittoria_next), .Q(out_3[1]));  // open: Qn, preset, en, reset
  D_Flip_Flop d_ff_2 (.clk(clock_1_out), .D(temponext_1_tempo_next), .Q(out_3[0]));  // open: Qn, preset, en, reset
endmodule

module VittoriaNext (
  input  stato_0,
  input  stato_1,
  input  Vittoria,
  input  Tempo,
  output Vittoria_next
);

  wire and_1_out, and_2_out;

  and and_1 (and_1_out, ~stato_0, ~stato_1, Vittoria, ~Tempo);  // AND_Gate
  and and_2 (and_2_out, stato_0, ~stato_1, Vittoria, ~Tempo);  // AND_Gate
  or or_1 (Vittoria_next, and_1_out, and_2_out);
endmodule

module TempoNext (
  input  stato_0,
  input  stato_1,
  input  Vittoria,
  input  Tempo,
  output Tempo_next
);

  wire and_1_out, and_2_out;

  and and_1 (and_1_out, ~stato_0, ~stato_1, ~Vittoria, Tempo);  // AND_Gate
  and and_2 (and_2_out, ~stato_0, stato_1, ~Vittoria, Tempo);  // AND_Gate
  or or_1 (Tempo_next, and_1_out, and_2_out);
endmodule

module DecideDisegno (
  input  [1:0] Disegno,
  input  [31:0] in_2,
  input  [31:0] in_3,
  input  [31:0] in_4,
  input  [31:0] in_5,
  input  [31:0] in_6,
  input  [31:0] in_7,
  input  [31:0] in_8,
  input  [31:0] in_9,
  input  [31:0] in_10,
  input  [31:0] in_11,
  input  [31:0] in_12,
  input  [31:0] in_13,
  input  [31:0] in_14,
  input  [31:0] in_15,
  input  [31:0] in_16,
  input  [31:0] in_17,
  input  [31:0] in_18,
  input  [31:0] in_19,
  input  [31:0] in_20,
  input  [31:0] in_21,
  input  [31:0] in_22,
  input  [31:0] in_23,
  input  [31:0] in_24,
  input  [31:0] in_25,
  input  [31:0] in_26,
  input  [31:0] in_27,
  input  [31:0] in_28,
  input  [31:0] in_29,
  input  [31:0] in_30,
  input  [31:0] in_31,
  input  [31:0] in_32,
  input  [31:0] in_33,
  input  [31:0] in_34,
  input  [31:0] in_35,
  input  [31:0] in_36,
  input  [31:0] in_37,
  input  [31:0] in_38,
  input  [31:0] in_39,
  input  [31:0] in_40,
  input  [31:0] in_41,
  input  [31:0] in_42,
  input  [31:0] in_43,
  input  [31:0] in_44,
  input  [31:0] in_45,
  input  [31:0] in_46,
  input  [31:0] in_47,
  input  [31:0] in_48,
  input  [31:0] in_49,
  input  [31:0] in_50,
  input  [31:0] in_51,
  input  [31:0] in_52,
  input  [31:0] in_53,
  input  [31:0] in_54,
  input  [31:0] in_55,
  input  [31:0] in_56,
  input  [31:0] in_57,
  input  [31:0] in_58,
  input  [31:0] in_59,
  input  [31:0] in_60,
  input  [31:0] in_61,
  input  [31:0] in_62,
  input  [31:0] in_63,
  input  [31:0] in_64,
  input  [31:0] in_65,
  input  [31:0] in_66,
  input  [31:0] in_67,
  input  [31:0] in_68,
  input  [31:0] in_69,
  input  [31:0] in_70,
  input  [31:0] in_71,
  input  [31:0] in_72,
  input  [31:0] in_73,
  input  [31:0] in_74,
  input  [31:0] in_75,
  input  [31:0] in_76,
  input  [31:0] in_77,
  input  [31:0] in_78,
  input  [31:0] in_79,
  input  [31:0] in_80,
  input  [31:0] in_81,
  input  [31:0] in_82,
  input  [31:0] in_83,
  input  [31:0] in_84,
  input  [31:0] in_85,
  input  [31:0] in_86,
  input  [31:0] in_87,
  input  [31:0] in_88,
  input  [31:0] in_89,
  input  [31:0] in_90,
  input  [31:0] in_91,
  input  [31:0] in_92,
  input  [31:0] in_93,
  input  [31:0] in_94,
  input  [31:0] in_95,
  input  [31:0] in_96,
  input  [31:0] in_97,
  input  [31:0] in_98,
  input  [31:0] in_99,
  input  [31:0] in_100,
  input  [31:0] in_101,
  input  [31:0] in_102,
  input  [31:0] in_103,
  input  [31:0] ultimo_in_game,
  input  [31:0] in_105,
  input  [31:0] in_106,
  input  [31:0] in_107,
  input  [31:0] in_108,
  input  [31:0] in_109,
  input  [31:0] in_110,
  input  [31:0] ultimo_lost,
  input  [31:0] in_112,
  input  [31:0] in_113,
  input  [31:0] in_114,
  input  [31:0] in_115,
  input  [31:0] in_116,
  input  [31:0] in_117,
  input  [31:0] ultimo_won,
  output [31:0] out_119,
  output [31:0] out_120,
  output [31:0] out_121,
  output [31:0] out_122,
  output [31:0] out_123,
  output [31:0] out_124,
  output [31:0] out_125,
  output [31:0] out_126,
  output [31:0] out_127,
  output [31:0] out_128,
  output [31:0] out_129,
  output [31:0] out_130,
  output [31:0] out_131,
  output [31:0] out_132,
  output [31:0] out_133,
  output [31:0] out_134,
  output [31:0] out_135,
  output [31:0] out_136,
  output [31:0] out_137,
  output [31:0] out_138,
  output [31:0] out_139,
  output [31:0] out_140,
  output [31:0] out_141,
  output [31:0] out_142,
  output [31:0] out_143,
  output [31:0] out_144,
  output [31:0] out_145,
  output [31:0] out_146,
  output [31:0] out_147,
  output [31:0] out_148,
  output [31:0] out_149,
  output [31:0] out_150,
  output [31:0] out_151,
  output [31:0] out_152,
  output [31:0] out_153,
  output [31:0] out_154,
  output [31:0] out_155,
  output [31:0] out_156,
  output [31:0] ultimo
);

  Multiplexer #(.select(2), .width(32)) multiplexer_1 (
    .in0(in_2), .in1(in_34), .in2(in_66), .out(out_119), .sel(Disegno));  // open: in3, en
  Multiplexer #(.select(2), .width(32)) multiplexer_2 (
    .in0(in_3), .in1(in_35), .in2(in_67), .out(out_120), .sel(Disegno));  // open: in3, en
  Multiplexer #(.select(2), .width(32)) multiplexer_3 (
    .in0(in_4), .in1(in_36), .in2(in_68), .out(out_121), .sel(Disegno));  // open: in3, en
  Multiplexer #(.select(2), .width(32)) multiplexer_4 (
    .in0(in_5), .in1(in_37), .in2(in_69), .out(out_122), .sel(Disegno));  // open: in3, en
  Multiplexer #(.select(2), .width(32)) multiplexer_5 (
    .in0(in_6), .in1(in_38), .in2(in_70), .out(out_123), .sel(Disegno));  // open: in3, en
  Multiplexer #(.select(2), .width(32)) multiplexer_6 (
    .in0(in_7), .in1(in_39), .in2(in_71), .out(out_124), .sel(Disegno));  // open: in3, en
  Multiplexer #(.select(2), .width(32)) multiplexer_7 (
    .in0(in_8), .in1(in_40), .in2(in_72), .out(out_125), .sel(Disegno));  // open: in3, en
  Multiplexer #(.select(2), .width(32)) multiplexer_8 (
    .in0(in_9), .in1(in_41), .in2(in_73), .out(out_126), .sel(Disegno));  // open: in3, en
  Multiplexer #(.select(2), .width(32)) multiplexer_9 (
    .in0(in_10), .in1(in_42), .in2(in_74), .out(out_127), .sel(Disegno));  // open: in3, en
  Multiplexer #(.select(2), .width(32)) multiplexer_10 (
    .in0(in_11), .in1(in_43), .in2(in_75), .out(out_128), .sel(Disegno));  // open: in3, en
  Multiplexer #(.select(2), .width(32)) multiplexer_11 (
    .in0(in_12), .in1(in_44), .in2(in_76), .out(out_129), .sel(Disegno));  // open: in3, en
  Multiplexer #(.select(2), .width(32)) multiplexer_12 (
    .in0(in_13), .in1(in_45), .in2(in_77), .out(out_130), .sel(Disegno));  // open: in3, en
  Multiplexer #(.select(2), .width(32)) multiplexer_13 (
    .in0(in_14), .in1(in_46), .in2(in_78), .out(out_131), .sel(Disegno));  // open: in3, en
  Multiplexer #(.select(2), .width(32)) multiplexer_14 (
    .in0(in_15), .in1(in_47), .in2(in_79), .out(out_132), .sel(Disegno));  // open: in3, en
  Multiplexer #(.select(2), .width(32)) multiplexer_15 (
    .in0(in_16), .in1(in_48), .in2(in_80), .out(out_133), .sel(Disegno));  // open: in3, en
  Multiplexer #(.select(2), .width(32)) multiplexer_16 (
    .in0(in_17), .in1(in_49), .in2(in_81), .out(out_134), .sel(Disegno));  // open: in3, en
  Multiplexer #(.select(2), .width(32)) multiplexer_17 (
    .in0(in_18), .in1(in_50), .in2(in_82), .out(out_135), .sel(Disegno));  // open: in3, en
  Multiplexer #(.select(2), .width(32)) multiplexer_18 (
    .in0(in_19), .in1(in_51), .in2(in_83), .out(out_136), .sel(Disegno));  // open: in3, en
  Multiplexer #(.select(2), .width(32)) multiplexer_19 (
    .in0(in_20), .in1(in_52), .in2(in_84), .out(out_137), .sel(Disegno));  // open: in3, en
  Multiplexer #(.select(2), .width(32)) multiplexer_20 (
    .in0(in_21), .in1(in_53), .in2(in_85), .out(out_138), .sel(Disegno));  // open: in3, en
  Multiplexer #(.select(2), .width(32)) multiplexer_21 (
    .in0(in_22), .in1(in_54), .in2(in_86), .out(out_139), .sel(Disegno));  // open: in3, en
  Multiplexer #(.select(2), .width(32)) multiplexer_22 (
    .in0(in_23), .in1(in_55), .in2(in_87), .out(out_140), .sel(Disegno));  // open: in3, en
  Multiplexer #(.select(2), .width(32)) multiplexer_23 (
    .in0(in_24), .in1(in_56), .in2(in_88), .out(out_141), .sel(Disegno));  // open: in3, en
  Multiplexer #(.select(2), .width(32)) multiplexer_24 (
    .in0(in_25), .in1(in_57), .in2(in_89), .out(out_142), .sel(Disegno));  // open: in3, en
  Multiplexer #(.select(2), .width(32)) multiplexer_25 (
    .in0(in_26), .in1(in_58), .in2(in_90), .out(out_143), .sel(Disegno));  // open: in3, en
  Multiplexer #(.select(2), .width(32)) multiplexer_26 (
    .in0(in_27), .in1(in_59), .in2(in_91), .out(out_144), .sel(Disegno));  // open: in3, en
  Multiplexer #(.select(2), .width(32)) multiplexer_27 (
    .in0(in_28), .in1(in_60), .in2(in_92), .out(out_145), .sel(Disegno));  // open: in3, en
  Multiplexer #(.select(2), .width(32)) multiplexer_28 (
    .in0(in_29), .in1(in_61), .in2(in_93), .out(out_146), .sel(Disegno));  // open: in3, en
  Multiplexer #(.select(2), .width(32)) multiplexer_29 (
    .in0(in_30), .in1(in_62), .in2(in_94), .out(out_147), .sel(Disegno));  // open: in3, en
  Multiplexer #(.select(2), .width(32)) multiplexer_30 (
    .in0(in_31), .in1(in_63), .in2(in_95), .out(out_148), .sel(Disegno));  // open: in3, en
  Multiplexer #(.select(2), .width(32)) multiplexer_31 (
    .in0(in_32), .in1(in_64), .in2(in_96), .out(out_149), .sel(Disegno));  // open: in3, en
  Multiplexer #(.select(2), .width(32)) multiplexer_32 (
    .in0(in_33), .in1(in_65), .in2(in_97), .out(out_150), .sel(Disegno));  // open: in3, en
  DotMatrix #(.matrixcols(32), .matrixrows(32)) dotmatrix_1 (
    .col0(out_119), .col1(out_120), .col2(out_121), .col3(out_122), .col4(out_123), .col5(out_124),
    .col6(out_125), .col7(out_126), .col8(out_127), .col9(out_128), .col10(out_129), .col11(out_130),
    .col12(out_131), .col13(out_132), .col14(out_133), .col15(out_134), .col16(out_135), .col17(out_136),
    .col18(out_137), .col19(out_138), .col20(out_139), .col21(out_140), .col22(out_141), .col23(out_142),
    .col24(out_143), .col25(out_144), .col26(out_145), .col27(out_146), .col28(out_147), .col29(out_148),
    .col30(out_149), .col31(out_150));
  Multiplexer #(.select(2), .width(32)) multiplexer_33 (
    .in0(in_98), .in1(in_105), .in2(in_112), .out(out_151), .sel(Disegno));  // open: in3, en
  Multiplexer #(.select(2), .width(32)) multiplexer_34 (
    .in0(in_99), .in1(in_106), .in2(in_113), .out(out_152), .sel(Disegno));  // open: in3, en
  Multiplexer #(.select(2), .width(32)) multiplexer_35 (
    .in0(in_100), .in1(in_107), .in2(in_114), .out(out_153), .sel(Disegno));  // open: in3, en
  Multiplexer #(.select(2), .width(32)) multiplexer_36 (
    .in0(in_101), .in1(in_108), .in2(in_115), .out(out_154), .sel(Disegno));  // open: in3, en
  Multiplexer #(.select(2), .width(32)) multiplexer_37 (
    .in0(in_102), .in1(in_109), .in2(in_116), .out(out_155), .sel(Disegno));  // open: in3, en
  Multiplexer #(.select(2), .width(32)) multiplexer_38 (
    .in0(in_103), .in1(in_110), .in2(in_117), .out(out_156), .sel(Disegno));  // open: in3, en
  Multiplexer #(.select(2), .width(32)) multiplexer_39 (
    .in0(ultimo_in_game), .in1(ultimo_lost), .in2(ultimo_won), .out(ultimo), .sel(Disegno));  // open: in3, en
  DotMatrix #(.matrixcols(7), .matrixrows(32)) dotmatrix_2 (
    .col0(out_151), .col1(out_152), .col2(out_153), .col3(out_154), .col4(out_155), .col5(out_156),
    .col6(ultimo));

  // Other names for the same wires on the sheet: _1_1[31:0] = in_2; _1_2[31:0] = in_3; _1_3[31:0] = in_4;
  //   _1_4[31:0] = in_5; _1_5[31:0] = in_6; _1_6[31:0] = in_7; _1_7[31:0] = in_8; _1_8[31:0] = in_9;
  //   _1_9[31:0] = in_10; _1_10[31:0] = in_11; _1_11[31:0] = in_12; _1_12[31:0] = in_13; _1_13[31:0] = in_14;
  //   _1_14[31:0] = in_15; _1_15[31:0] = in_16; _1_16[31:0] = in_17; _1_17[31:0] = in_18; _1_18[31:0] = in_19;
  //   _1_19[31:0] = in_20; _1_20[31:0] = in_21; _1_21[31:0] = in_22; _1_22[31:0] = in_23; _1_23[31:0] = in_24;
  //   _1_24[31:0] = in_25; _1_25[31:0] = in_26; _1_26[31:0] = in_27; _1_27[31:0] = in_28; _1_28[31:0] = in_29;
  //   _1_29[31:0] = in_30; _1_30[31:0] = in_31; _1_31[31:0] = in_32; _1_32[31:0] = in_33; _2_1[31:0] = in_34;
  //   _2_2[31:0] = in_35; _2_3[31:0] = in_36; _2_4[31:0] = in_37; _2_5[31:0] = in_38; _2_6[31:0] = in_39;
  //   _2_7[31:0] = in_40; _2_8[31:0] = in_41; _2_9[31:0] = in_42; _2_10[31:0] = in_43; _2_11[31:0] = in_44;
  //   _2_12[31:0] = in_45; _2_13[31:0] = in_46; _2_14[31:0] = in_47; _2_15[31:0] = in_48; _2_16[31:0] = in_49;
  //   _2_17[31:0] = in_50; _2_18[31:0] = in_51; _2_19[31:0] = in_52; _2_20[31:0] = in_53; _2_21[31:0] = in_54;
  //   _2_22[31:0] = in_55; _2_23[31:0] = in_56; _2_24[31:0] = in_57; _2_25[31:0] = in_58; _2_26[31:0] = in_59;
  //   _2_27[31:0] = in_60; _2_28[31:0] = in_61; _2_29[31:0] = in_62; _2_30[31:0] = in_63; _2_31[31:0] = in_64;
  //   _2_32[31:0] = in_65; _3_1[31:0] = in_66; _3_2[31:0] = in_67; _3_3[31:0] = in_68; _3_4[31:0] = in_69;
  //   _3_5[31:0] = in_70; _3_6[31:0] = in_71; _3_7[31:0] = in_72; _3_8[31:0] = in_73; _3_9[31:0] = in_74;
  //   _3_10[31:0] = in_75; _3_11[31:0] = in_76; _3_12[31:0] = in_77; _3_13[31:0] = in_78; _3_14[31:0] = in_79;
  //   _3_15[31:0] = in_80; _3_16[31:0] = in_81; _3_17[31:0] = in_82; _3_18[31:0] = in_83; _3_19[31:0] = in_84;
  //   _3_20[31:0] = in_85; _3_21[31:0] = in_86; _3_22[31:0] = in_87; _3_23[31:0] = in_88; _3_24[31:0] = in_89;
  //   _3_25[31:0] = in_90; _3_26[31:0] = in_91; _3_27[31:0] = in_92; _3_28[31:0] = in_93; _3_29[31:0] = in_94;
  //   _3_30[31:0] = in_95; _3_31[31:0] = in_96; _3_32[31:0] = in_97; _4_1[31:0] = in_98; _4_2[31:0] = in_99;
  //   _4_3[31:0] = in_100; _4_4[31:0] = in_101; _4_5[31:0] = in_102; _4_6[31:0] = in_103; _4_7[31:0] = ultimo_in_game;
  //   _5_1[31:0] = in_105; _5_2[31:0] = in_106; _5_3[31:0] = in_107; _5_4[31:0] = in_108; _5_5[31:0] = in_109;
  //   _5_6[31:0] = in_110; _5_7[31:0] = ultimo_lost; _6_1[31:0] = in_112; _6_2[31:0] = in_113; _6_3[31:0] = in_114;
  //   _6_4[31:0] = in_115; _6_5[31:0] = in_116; _6_6[31:0] = in_117; _6_7[31:0] = ultimo_won

  // Notes on the sheet:
  //   Scritta:
endmodule

module won (
  output [31:0] out_1,
  output [31:0] out_2,
  output [31:0] out_3,
  output [31:0] out_4,
  output [31:0] out_5,
  output [31:0] out_6,
  output [31:0] ultimo
);

  DotMatrix #(.matrixcols(7), .matrixrows(32)) dotmatrix_1 (
    .col0(32'hfe0f83fc), .col1(32'h1104100), .col2(32'h2202180), .col3(32'h1c202060), .col4(32'h2202010),
    .col5(32'h1104008), .col6(32'hfe0f83fc));

  assign out_1 = 32'hfe0f83fc;
  assign out_2 = 32'h1104100;
  assign out_3 = 32'h2202180;
  assign out_4 = 32'h1c202060;
  assign out_5 = 32'h2202010;
  assign out_6 = 32'h1104008;
  assign ultimo = 32'hfe0f83fc;
endmodule

module lost (
  output [31:0] out_1,
  output [31:0] out_2,
  output [31:0] out_3,
  output [31:0] out_4,
  output [31:0] out_5,
  output [31:0] out_6,
  output [31:0] ultimo
);

  DotMatrix #(.matrixcols(7), .matrixrows(32)) dotmatrix_1 (
    .col0(32'h706400), .col1(32'hfc889280), .col2(32'h5049280), .col3(32'h50492fe), .col4(32'h5049280),
    .col5(32'h4889280), .col6(32'h704c00));

  assign out_1 = 32'h706400;
  assign out_2 = 32'hfc889280;
  assign out_3 = 32'h5049280;
  assign out_4 = 32'h50492fe;
  assign out_5 = 32'h5049280;
  assign out_6 = 32'h4889280;
  assign ultimo = 32'h704c00;
endmodule

module in_game (
  output [31:0] out_1,
  output [31:0] out_2,
  output [31:0] out_3,
  output [31:0] out_4,
  output [31:0] out_5,
  output [31:0] out_6,
  output [31:0] ultimo
);

  DotMatrix #(.matrixcols(7), .matrixrows(32)) dotmatrix_1 (
    .col0({32{1'b0}}), .col1({32{1'b0}}), .col2({32{1'b0}}), .col3({32{1'b0}}), .col4({32{1'b0}}),
    .col5({32{1'b0}}), .col6({32{1'b0}}));

  assign out_1 = {32{1'b0}};
  assign out_2 = {32{1'b0}};
  assign out_3 = {32{1'b0}};
  assign out_4 = {32{1'b0}};
  assign out_5 = {32{1'b0}};
  assign out_6 = {32{1'b0}};
  assign ultimo = {32{1'b0}};
endmodule
